# Fritzing sketch ATtiny84_programmer (saved by Fritzing 0.9.3b)
circuit board: 8.46667cm x 5.64444cm
breadboards: 1

parts:
  Componente1 = Arduino Nano (Rev3.0)
  Componente2 = ATtiny 44 [package="DIP14 [THT]"]
  LED1 = LED - 5mm [color="Red (633nm)" package="5 mm [THT]"]
  R1 = Resistor [tolerance=±5% resistance=100 package=THT]
  C1 = Electrolytic Capacitor [capacitance=1µF package="100 mil [THT, electrolytic]"]

nets:
  N1: Componente1.RESET, C1.+
  GND: Componente1.GND, Componente2.GND, R1.Pin_0, C1.-
  N2: Componente1.D10, Componente2.Reset
  N3: Componente1.D11/MOSI, Componente2.Pin_6
  N4: Componente1.D12/MISO, Componente2.Pin_5
  N5: Componente1.5V, Componente2.Vcc_(+)
  N6: Componente1.D13/SCK, Componente2.Pin_4
  N7: Componente2.Pin_10, LED1.anode
  N8: LED1.cathode, R1.Pin_1

custom parts:
  ATtiny 44: ATtiny 44 Microcontroller
